// Logisim project up_down_counter.circ as structural Verilog: 5 circuits, main circuit convert_bcd
module convert_bcd (
  input  D3,
  input  D2,
  input  D1,
  input  D0,
  output a,
  output b,
  output c,
  output d,
  output e,
  output f,
  output g
);

  wire and_1_out, and_2_out, and_3_out, and_4_out, and_5_out, and_6_out, and_7_out, and_8_out, and_9_out,
       and_10_out, and_11_out, and_12_out, and_13_out, and_14_out, and_15_out, and_16_out, and_17_out,
       and_18_out, and_19_out, and_20_out, and_21_out, and_22_out, and_23_out, and_24_out, and_25_out,
       not_1_out, not_2_out, not_3_out, not_4_out, not_5_out, not_6_out, not_7_out, not_8_out, not_9_out,
       not_10_out, not_11_out, not_12_out, not_13_out, not_14_out, not_15_out, not_16_out, not_17_out,
       not_18_out, not_19_out, not_20_out, not_21_out, not_22_out, not_23_out, not_24_out, not_25_out,
       not_26_out, not_27_out, not_28_out, not_29_out, not_30_out, not_31_out, not_32_out, not_33_out,
       not_34_out, not_35_out, not_36_out, not_37_out, not_38_out, not_39_out, not_40_out, not_41_out;

  not not_1 (not_1_out, D3);
  not not_2 (not_2_out, D2);
  not not_3 (not_3_out, D1);
  not not_4 (not_4_out, D3);
  not not_5 (not_5_out, D1);
  not not_6 (not_6_out, D0);
  not not_7 (not_7_out, D2);
  not not_8 (not_8_out, D1);
  not not_9 (not_9_out, D3);
  not not_10 (not_10_out, D1);
  not not_11 (not_11_out, D0);
  not not_12 (not_12_out, D0);
  not not_13 (not_13_out, D3);
  not not_14 (not_14_out, D2);
  not not_15 (not_15_out, D0);
  not not_16 (not_16_out, D0);
  not not_17 (not_17_out, D3);
  not not_18 (not_18_out, D2);
  not not_19 (not_19_out, D1);
  not not_20 (not_20_out, D3);
  not not_21 (not_21_out, D1);
  not not_22 (not_22_out, D0);
  not not_23 (not_23_out, D2);
  not not_24 (not_24_out, D0);
  not not_25 (not_25_out, D3);
  and and_1 (and_1_out, not_25_out, D0);
  not not_26 (not_26_out, D2);
  not not_27 (not_27_out, D1);
  and and_2 (and_2_out, not_26_out, not_27_out, D0);
  not not_28 (not_28_out, D3);
  and and_3 (and_3_out, not_28_out, D2, not_29_out);
  not not_29 (not_29_out, D1);
  not not_30 (not_30_out, D3);
  not not_31 (not_31_out, D2);
  not not_32 (not_32_out, D3);
  not not_33 (not_33_out, D2);
  not not_34 (not_34_out, D3);
  not not_35 (not_35_out, D1);
  not not_36 (not_36_out, D3);
  not not_37 (not_37_out, D2);
  not not_38 (not_38_out, D1);
  not not_39 (not_39_out, D3);
  not not_40 (not_40_out, D1);
  not not_41 (not_41_out, D0);
  and and_4 (and_4_out, not_1_out, not_2_out, not_3_out, D0);
  and and_5 (and_5_out, not_4_out, D2, not_5_out, not_6_out);
  and and_6 (and_6_out, D3, not_7_out, D1, D0);
  and and_7 (and_7_out, D3, D2, not_8_out, D0);
  and and_8 (and_8_out, not_9_out, D2, not_10_out, D0);
  and and_9 (and_9_out, D2, D1, not_11_out);
  and and_10 (and_10_out, D3, D1, D0);
  and and_11 (and_11_out, D3, D2, not_12_out);
  and and_12 (and_12_out, not_13_out, not_14_out, D1, not_15_out);
  and and_13 (and_13_out, D3, D2, not_16_out);
  or or_1 (c, and_12_out, and_13_out, and_14_out);
  and and_14 (and_14_out, D3, D2, D1);
  and and_15 (and_15_out, not_17_out, not_18_out, not_19_out, D0);
  and and_16 (and_16_out, not_20_out, D2, not_21_out, not_22_out);
  and and_17 (and_17_out, D2, D1, D0);
  and and_18 (and_18_out, D3, not_23_out, D1, not_24_out);
  or or_2 (e, and_1_out, and_2_out, and_3_out);
  and and_19 (and_19_out, not_30_out, not_31_out, D0);
  and and_20 (and_20_out, not_32_out, not_33_out, D1);
  and and_21 (and_21_out, not_34_out, D1, D0);
  and and_22 (and_22_out, D3, D2, not_35_out, D0);
  and and_23 (and_23_out, not_36_out, not_37_out, not_38_out);
  or or_3 (g, and_23_out, and_24_out, and_25_out);
  and and_24 (and_24_out, not_39_out, D2, D1, D0);
  and and_25 (and_25_out, D3, D2, not_40_out, not_41_out);
  or or_4 (a, and_4_out, and_5_out, and_6_out, and_7_out);
  or or_5 (b, and_8_out, and_9_out, and_10_out, and_11_out);
  or or_6 (d, and_15_out, and_16_out, and_17_out, and_18_out);
  or or_7 (f, and_19_out, and_20_out, and_21_out, and_22_out);
endmodule

module clock_v2 (
);

  wire and_1_out, and_2_out, and_3_out, and_4_out, and_5_out, and_6_out, and_7_out, and_8_out, and_9_out,
       and_10_out, and_11_out, and_12_out, and_13_out, and_14_out, and_15_out, and_16_out, and_17_out,
       and_18_out, and_19_out, and_20_out, and_21_out, and_22_out, and_23_out, and_24_out, and_25_out,
       and_26_out, and_27_out, and_28_out, and_29_out, and_30_out, and_31_out, and_32_out, and_33_out,
       and_34_out, and_35_out, and_36_out, and_37_out, and_38_out, and_39_out, and_40_out, and_41_out,
       and_42_out, and_43_out, and_44_out, and_46_out, and_47_out, and_48_out, and_50_out, and_51_out,
       and_52_out, and_53_out, clock_1_out, clock_2_out, clock_3_out, clock_4_out, clock_5_out, clock_6_out,
       comp, comp1, COMP_out, convert_bcd_1_a, convert_bcd_1_b, convert_bcd_1_c, convert_bcd_1_d,
       convert_bcd_1_e, convert_bcd_1_f, convert_bcd_1_g, convert_bcd_2_a, convert_bcd_2_b, convert_bcd_2_c,
       convert_bcd_2_d, convert_bcd_2_e, convert_bcd_2_f, convert_bcd_2_g, convert_bcd_3_a, convert_bcd_3_b,
       convert_bcd_3_c, convert_bcd_3_d, convert_bcd_3_e, convert_bcd_3_f, convert_bcd_3_g, convert_bcd_4_a,
       convert_bcd_4_b, convert_bcd_4_c, convert_bcd_4_d, convert_bcd_4_e, convert_bcd_4_f, convert_bcd_4_g,
       convert_bcd_5_a, convert_bcd_5_b, convert_bcd_5_c, convert_bcd_5_d, convert_bcd_5_e, convert_bcd_5_f,
       convert_bcd_5_g, convert_bcd_6_a, convert_bcd_6_b, convert_bcd_6_c, convert_bcd_6_d, convert_bcd_6_e,
       convert_bcd_6_f, convert_bcd_6_g, d_ff_1_q, d_ff_2_q, d_ff_3_q, d_ff_4_q, d_ff_5_q, d_ff_6_q,
       d_ff_7_q, d_ff_8_q, d_ff_9_q, d_ff_10_q, d_ff_11_qn, d_ff_12_qn, DONE, multiplexer_1_out,
       multiplexer_2_out, multiplexer_3_out, multiplexer_4_out, multiplexer_5_out, multiplexer_6_out,
       multiplexer_7_out, multiplexer_8_out, nor_1_out, nor_2_out, not_1_out, not_2_out, not_3_out, or_1_out,
       or_2_out, or_4_out, or_5_out, or_6_out, or_7_out, or_8_out, or_9_out, or_10_out, or_11_out, or_12_out,
       or_13_out, or_14_out, or_15_out, or_16_out, or_17_out, or_18_out, or_19_out, or_20_out, or_21_out,
       or_22_out, or_23_out, or_24_out, or_25_out, or_26_out, or_27_out, or_28_out, or_29_out, or_30_out,
       or_31_out, or_32_out, or_33_out, or_34_out, or_35_out, or_36_out, or_37_out, or_38_out, or_39_out,
       or_40_out, or_41_out, pull_resistor_1_node, pull_resistor_2_node, Q0, Q0_prime, Q0N, Q0N_prime, Q1,
       Q1_prime, Q1N, Q1N_prime, Q2, Q2_prime, Q2N, Q2N_prime, Q3, Q3_prime, Q3N, Q3N_prime, Q4, Q4_prime,
       Q5, Q5_prime, Q6, Q6_prime, Q7, Q7_prime, Q8, Q8_prime, Q9, Q9_prime, Q10, Q10_prime, RESET,
       RESET_out, set, set_prime, start, t_ff_2_qn, t_ff_5_qn, t_ff_6_q, trigger, trigger_prime, up, update,
       update_prime;

  Clock clock_1 (.out(clock_1_out));
  toogle_sig toogle_sig_1 (.in_1(COMP_out), .in_2(RESET), .out_3(comp), .out_4(comp1));
  Button u_RESET (.out(RESET_out));
  D_Flip_Flop d_ff_1 (.clk(comp), .D(1'b1), .Q(d_ff_1_q), .reset(d_ff_7_q));  // open: Qn, preset, en
  Clock clock_2 (.out(clock_2_out));
  D_Flip_Flop d_ff_2 (.clk(comp), .D(1'b1), .Q(d_ff_2_q), .reset(d_ff_5_q));  // open: Qn, preset, en
  D_Flip_Flop d_ff_3 (.clk(comp1), .D(1'b1), .Q(d_ff_3_q), .reset(d_ff_9_q));  // open: Qn, preset, en
  Clock clock_3 (.out(clock_3_out));
  D_Flip_Flop d_ff_4 (.clk(comp1), .D(1'b1), .Q(d_ff_4_q), .reset(d_ff_6_q));  // open: Qn, preset, en
  Clock clock_4 (.out(clock_4_out));
  not not_1 (not_1_out, up);
  and and_1 (and_1_out, Q1, Q0);
  or or_1 (or_1_out, and_1_out, and_2_out);
  and and_2 (and_2_out, ~Q1, ~Q0);  // AND_Gate
  and and_3 (and_3_out, Q2, Q1);
  or or_2 (or_2_out, and_3_out, and_4_out, and_5_out);
  and and_4 (and_4_out, Q2, Q0);
  and and_5 (and_5_out, ~Q0, ~Q1, ~Q2);  // AND_Gate
  and and_6 (and_6_out, Q3, Q0);
  and and_7 (and_7_out, Q3, Q1);
  and and_8 (and_8_out, Q3, Q2);
  and and_9 (and_9_out, ~Q0, ~Q1, ~Q2, ~Q3);  // AND_Gate
  Button u_COMP (.out(COMP_out));
  or or_3 (RESET, RESET_out, DONE);
  D_Flip_Flop d_ff_5 (.clk(clock_1_out), .D(d_ff_2_q), .Q(d_ff_5_q), .reset(d_ff_8_q));  // open: Qn, preset, en
  and and_10 (and_10_out, Q1_prime, Q0_prime);
  and and_11 (and_11_out, ~Q1_prime, ~Q0_prime);  // AND_Gate
  and and_12 (and_12_out, Q2_prime, Q1_prime);
  and and_13 (and_13_out, Q2_prime, Q0_prime);
  and and_14 (and_14_out, ~Q0_prime, ~Q1_prime, ~Q2_prime);  // AND_Gate
  and and_15 (and_15_out, Q3_prime, Q0_prime);
  and and_16 (and_16_out, Q3_prime, Q1_prime);
  and and_17 (and_17_out, Q3_prime, Q2_prime);
  and and_18 (and_18_out, ~Q0_prime, ~Q1_prime, ~Q2_prime, ~Q3_prime);  // AND_Gate
  D_Flip_Flop d_ff_6 (.clk(clock_4_out), .D(d_ff_4_q), .Q(d_ff_6_q), .reset(d_ff_10_q));  // open: Qn, preset, en
  or or_4 (or_4_out, and_6_out, and_7_out, and_8_out, and_9_out);
  T_Flip_Flop t_ff_1 (.clk(COMP_out), .T(COMP_out), .Q(up));  // open: Qn, preset, reset, en
  Button u_START (.out(start));
  D_Flip_Flop d_ff_7 (.clk(clock_2_out), .D(d_ff_1_q), .Q(d_ff_7_q));  // open: Qn, preset, en, reset
  D_Flip_Flop d_ff_8 (.clk(clock_1_out), .D(d_ff_5_q), .Q(d_ff_8_q));  // open: Qn, preset, en, reset
  or or_5 (or_5_out, start, and_19_out);
  and and_19 (and_19_out, RESET, ~t_ff_2_qn);  // AND_Gate
  or or_6 (or_6_out, and_10_out, and_11_out);
  or or_7 (or_7_out, and_12_out, and_13_out, and_14_out);
  or or_8 (or_8_out, and_15_out, and_16_out, and_17_out, and_18_out);
  not not_2 (not_2_out, up);
  D_Flip_Flop d_ff_9 (.clk(clock_3_out), .D(d_ff_3_q), .Q(d_ff_9_q));  // open: Qn, preset, en, reset
  D_Flip_Flop d_ff_10 (.clk(clock_4_out), .D(d_ff_6_q), .Q(d_ff_10_q));  // open: Qn, preset, en, reset
  and and_20 (and_20_out, RESET, ~t_ff_5_qn);  // AND_Gate
  Multiplexer multiplexer_1 (.in0(d_ff_11_qn), .in1(Q0N), .out(multiplexer_1_out), .sel(up));  // open: en
  or or_9 (or_9_out, COMP_out, start);
  and and_21 (and_21_out, RESET, t_ff_6_q);
  and and_22 (and_22_out, d_ff_8_q, trigger);
  T_Flip_Flop t_ff_2 (.clk(or_5_out), .T(or_5_out), .Qn(t_ff_2_qn));  // open: Q, preset, reset, en
  Multiplexer multiplexer_2 (.in0(d_ff_12_qn), .in1(Q0N_prime), .out(multiplexer_2_out), .sel(not_2_out));  // open: en
  and and_23 (and_23_out, d_ff_10_q, trigger_prime);
  or or_10 (or_10_out, start, and_20_out);
  D_Flip_Flop d_ff_11 (
    .clk(or_24_out), .D(multiplexer_1_out), .Q(Q0), .Qn(d_ff_11_qn), .reset(RESET));  // open: preset, en
  or or_11 (or_11_out, or_9_out, and_21_out);
  or or_12 (or_12_out, update, and_22_out);
  T_Flip_Flop t_ff_3 (.clk(or_40_out), .T(1'b1), .Q(Q7), .reset(RESET));  // open: Qn, preset, en
  D_Flip_Flop d_ff_12 (
    .clk(or_27_out), .D(multiplexer_2_out), .Q(Q0_prime), .Qn(d_ff_12_qn), .reset(RESET));  // open: preset, en
  not not_3 (not_3_out, up);
  or or_13 (or_13_out, update_prime, and_23_out);
  T_Flip_Flop t_ff_4 (.clk(or_41_out), .T(1'b1), .Q(Q7_prime), .reset(RESET));  // open: Qn, preset, en
  T_Flip_Flop t_ff_5 (.clk(or_10_out), .T(or_10_out), .Qn(t_ff_5_qn));  // open: Q, preset, reset, en
  Clock clock_5 (.out(clock_5_out));
  T_Flip_Flop t_ff_6 (.clk(or_11_out), .T(or_11_out), .Q(t_ff_6_q), .reset(RESET));  // open: Qn, preset, en
  T_Flip_Flop t_ff_7 (.clk(or_12_out), .T(1'b1), .Q(Q4), .reset(RESET));  // open: Qn, preset, en
  and and_24 (and_24_out, ~Q7, ~up);  // AND_Gate
  and and_25 (and_25_out, Q7, up);
  T_Flip_Flop t_ff_8 (.clk(or_13_out), .T(1'b1), .Q(Q4_prime), .reset(RESET));  // open: Qn, preset, en
  and and_26 (and_26_out, ~Q7_prime, ~not_1_out);  // AND_Gate
  and and_27 (and_27_out, Q7_prime, not_1_out);
  Multiplexer multiplexer_3 (.in0(or_1_out), .in1(Q1N), .out(multiplexer_3_out), .sel(up));  // open: en
  or or_14 (or_14_out, RESET, update);
  Pull_Resistor pull_resistor_1 (.node(pull_resistor_1_node));
  Transistor #(.\type ("n")) transistor_1 (.in(clock_5_out), .out(pull_resistor_1_node), .gate(t_ff_6_q));
  and and_28 (and_28_out, ~Q4, ~up);  // AND_Gate
  or or_15 (or_15_out, and_28_out, and_29_out);
  and and_29 (and_29_out, Q4, up);
  or or_16 (or_16_out, and_24_out, and_25_out);
  T_Flip_Flop t_ff_9 (.clk(or_40_out), .T(or_16_out), .Q(Q8), .preset(t_ff_2_qn), .reset(or_17_out));  // open: Qn, en
  or or_17 (or_17_out, and_48_out, and_47_out);
  Multiplexer multiplexer_4 (.in0(or_6_out), .in1(Q1N_prime), .out(multiplexer_4_out), .sel(not_2_out));  // open: en
  Clock clock_6 (.out(clock_6_out));
  Pull_Resistor pull_resistor_2 (.node(pull_resistor_2_node));
  Transistor #(.\type ("n")) transistor_2 (.in(clock_6_out), .out(pull_resistor_2_node), .gate(comp));
  and and_30 (and_30_out, ~Q4_prime, ~not_3_out);  // AND_Gate
  or or_18 (or_18_out, and_30_out, and_31_out);
  and and_31 (and_31_out, Q4_prime, not_3_out);
  or or_19 (or_19_out, and_26_out, and_27_out);
  or or_20 (or_20_out, and_53_out, and_52_out);
  state_update state_update_1 (.Q3(Q3), .Q2(Q2), .Q1(Q1), .Q0(Q0), .add(trigger));
  D_Flip_Flop d_ff_13 (.clk(or_24_out), .D(multiplexer_3_out), .Q(Q1), .reset(or_14_out));  // open: Qn, preset, en
  T_Flip_Flop t_ff_10 (.clk(or_12_out), .T(or_15_out), .Q(Q5), .reset(or_21_out));  // open: Qn, preset, en
  or or_21 (or_21_out, RESET, and_46_out, and_40_out);
  and and_32 (and_32_out, ~Q8, ~Q7, ~up);  // AND_Gate
  and and_33 (and_33_out, Q8, Q7, up);
  D_Flip_Flop d_ff_14 (
    .clk(or_27_out), .D(multiplexer_4_out), .Q(Q1_prime), .reset(or_22_out));  // open: Qn, preset, en
  or or_22 (or_22_out, RESET, update_prime);
  T_Flip_Flop t_ff_11 (.clk(or_13_out), .T(or_18_out), .Q(Q5_prime), .reset(or_23_out));  // open: Qn, preset, en
  or or_23 (or_23_out, RESET, and_50_out, and_51_out);
  T_Flip_Flop t_ff_12 (
    .clk(or_41_out), .T(or_19_out), .Q(Q8_prime), .preset(t_ff_5_qn), .reset(or_20_out));  // open: Qn, en
  Multiplexer multiplexer_5 (.in0(or_2_out), .in1(Q2N), .out(multiplexer_5_out), .sel(up));  // open: en
  or or_24 (or_24_out, pull_resistor_1_node, d_ff_7_q);
  and and_34 (and_34_out, ~up, ~Q4, ~Q5);  // AND_Gate
  and and_35 (and_35_out, up, Q4, Q5);
  or or_25 (or_25_out, and_32_out, and_33_out);
  T_Flip_Flop t_ff_13 (.clk(or_40_out), .T(or_25_out), .Q(Q9), .reset(or_26_out));  // open: Qn, preset, en
  or or_26 (or_26_out, RESET, and_47_out);
  state_update state_update_2 (.Q3(Q3_prime), .Q2(Q2_prime), .Q1(Q1_prime), .Q0(Q0_prime), .add(trigger_prime));
  Multiplexer multiplexer_6 (.in0(or_7_out), .in1(Q2N_prime), .out(multiplexer_6_out), .sel(not_2_out));  // open: en
  or or_27 (or_27_out, pull_resistor_2_node, d_ff_9_q);
  and and_36 (and_36_out, ~not_3_out, ~Q4_prime, ~Q5_prime);  // AND_Gate
  and and_37 (and_37_out, not_3_out, Q4_prime, Q5_prime);
  and and_38 (and_38_out, ~Q8_prime, ~Q7_prime, ~not_1_out);  // AND_Gate
  or or_28 (or_28_out, and_38_out, and_39_out);
  and and_39 (and_39_out, Q8_prime, Q7_prime, not_1_out);
  T_Flip_Flop t_ff_14 (.clk(or_41_out), .T(or_28_out), .Q(Q9_prime), .reset(or_29_out));  // open: Qn, preset, en
  or or_29 (or_29_out, RESET, and_52_out);
  D_Flip_Flop d_ff_15 (.clk(or_24_out), .D(multiplexer_5_out), .Q(Q2), .reset(or_30_out));  // open: Qn, preset, en
  or or_30 (or_30_out, RESET, update);
  or or_31 (or_31_out, and_34_out, and_35_out);
  D_Flip_Flop d_ff_16 (
    .clk(or_27_out), .D(multiplexer_6_out), .Q(Q2_prime), .reset(or_32_out));  // open: Qn, preset, en
  or or_32 (or_32_out, RESET, update_prime);
  or or_33 (or_33_out, and_36_out, and_37_out);
  add_3 add_3_1 (.Q3(Q3), .Q2(Q2), .Q1(Q1), .Q0(Q0), .Q3N(Q3N), .Q2N(Q2N), .Q1N(Q1N), .Q0N(Q0N), .carry(set));
  Multiplexer multiplexer_7 (.in0(or_4_out), .in1(Q3N), .out(multiplexer_7_out), .sel(up));  // open: en
  T_Flip_Flop t_ff_15 (.clk(or_12_out), .T(or_31_out), .Q(Q6), .reset(or_34_out));  // open: Qn, preset, en
  or or_34 (or_34_out, RESET, and_46_out);
  and and_40 (and_40_out, Q6, ~up, Q5);  // AND_Gate
  and and_41 (and_41_out, ~Q7, ~Q8, ~Q9, ~up);  // AND_Gate
  or or_35 (or_35_out, and_41_out, and_42_out);
  and and_42 (and_42_out, Q7, Q8, Q9, up);
  T_Flip_Flop t_ff_16 (.clk(or_40_out), .T(or_35_out), .Q(Q10), .reset(or_36_out));  // open: Qn, preset, en
  or or_36 (or_36_out, RESET, and_48_out);
  Multiplexer multiplexer_8 (.in0(or_8_out), .in1(Q3N_prime), .out(multiplexer_8_out), .sel(not_2_out));  // open: en
  T_Flip_Flop t_ff_17 (.clk(or_13_out), .T(or_33_out), .Q(Q6_prime), .reset(or_37_out));  // open: Qn, preset, en
  or or_37 (or_37_out, RESET, and_50_out);
  and and_43 (and_43_out, ~Q7_prime, ~Q8_prime, ~Q9_prime, ~not_1_out);  // AND_Gate
  or or_38 (or_38_out, and_43_out, and_44_out);
  and and_44 (and_44_out, Q7_prime, Q8_prime, Q9_prime, not_1_out);
  T_Flip_Flop t_ff_18 (.clk(or_41_out), .T(or_38_out), .Q(Q10_prime), .reset(or_39_out));  // open: Qn, preset, en
  or or_39 (or_39_out, RESET, and_53_out);
  D_Flip_Flop d_ff_17 (.clk(or_24_out), .D(multiplexer_7_out), .Q(Q3), .reset(RESET));  // open: Qn, preset, en
  and and_45 (update, Q3, Q1);
  and and_46 (and_46_out, Q6, up, Q5);
  and and_47 (and_47_out, Q8, ~up, Q10);  // AND_Gate
  and and_48 (and_48_out, Q8, up, Q10);
  add_3 add_3_2 (
    .Q3(Q3_prime), .Q2(Q2_prime), .Q1(Q1_prime), .Q0(Q0_prime), .Q3N(Q3N_prime), .Q2N(Q2N_prime),
    .Q1N(Q1N_prime), .Q0N(Q0N_prime), .carry(set_prime));
  D_Flip_Flop d_ff_18 (.clk(or_27_out), .D(multiplexer_8_out), .Q(Q3_prime), .reset(RESET));  // open: Qn, preset, en
  and and_49 (update_prime, Q3_prime, Q1_prime);
  and and_50 (and_50_out, Q6_prime, not_3_out, Q5_prime);
  and and_51 (and_51_out, Q6_prime, ~not_3_out, Q5_prime);  // AND_Gate
  and and_52 (and_52_out, Q8_prime, ~not_1_out, Q10_prime);  // AND_Gate
  or or_40 (or_40_out, and_40_out, and_46_out);
  or or_41 (or_41_out, and_51_out, and_50_out);
  and and_53 (and_53_out, Q8_prime, not_1_out, Q10_prime);
  convert_bcd convert_bcd_1 (
    .D3(Q10), .D2(Q9), .D1(Q8), .D0(Q7), .a(convert_bcd_1_a), .b(convert_bcd_1_b), .c(convert_bcd_1_c),
    .d(convert_bcd_1_d), .e(convert_bcd_1_e), .f(convert_bcd_1_f), .g(convert_bcd_1_g));
  convert_bcd convert_bcd_2 (
    .D3(1'b0), .D2(Q6), .D1(Q5), .D0(Q4), .a(convert_bcd_2_a), .b(convert_bcd_2_b), .c(convert_bcd_2_c),
    .d(convert_bcd_2_d), .e(convert_bcd_2_e), .f(convert_bcd_2_f), .g(convert_bcd_2_g));
  convert_bcd convert_bcd_3 (
    .D3(Q3), .D2(Q2), .D1(Q1), .D0(Q0), .a(convert_bcd_3_a), .b(convert_bcd_3_b), .c(convert_bcd_3_c),
    .d(convert_bcd_3_d), .e(convert_bcd_3_e), .f(convert_bcd_3_f), .g(convert_bcd_3_g));
  nor nor_1 (nor_1_out, Q10, Q9, Q8, Q7, Q6, Q5, Q4, Q3, Q2, Q1, Q0);
  _7_Segment_Display #(.active("false")) u_7_segment_display_1 (
    .g(convert_bcd_1_g), .f(convert_bcd_1_f), .a(convert_bcd_1_a), .b(convert_bcd_1_b), .e(convert_bcd_1_e),
    .d(convert_bcd_1_d), .c(convert_bcd_1_c));  // open: dp
  _7_Segment_Display #(.active("false")) u_7_segment_display_2 (
    .g(convert_bcd_2_g), .f(convert_bcd_2_f), .a(convert_bcd_2_a), .b(convert_bcd_2_b), .e(convert_bcd_2_e),
    .d(convert_bcd_2_d), .c(convert_bcd_2_c));  // open: dp
  _7_Segment_Display #(.active("false")) u_7_segment_display_3 (
    .g(convert_bcd_3_g), .f(convert_bcd_3_f), .a(convert_bcd_3_a), .b(convert_bcd_3_b), .e(convert_bcd_3_e),
    .d(convert_bcd_3_d), .c(convert_bcd_3_c));  // open: dp
  or or_42 (DONE, nor_1_out, nor_2_out);
  convert_bcd convert_bcd_4 (
    .D3(Q10_prime), .D2(Q9_prime), .D1(Q8_prime), .D0(Q7_prime), .a(convert_bcd_4_a), .b(convert_bcd_4_b),
    .c(convert_bcd_4_c), .d(convert_bcd_4_d), .e(convert_bcd_4_e), .f(convert_bcd_4_f), .g(convert_bcd_4_g));
  convert_bcd convert_bcd_5 (
    .D3(1'b0), .D2(Q6_prime), .D1(Q5_prime), .D0(Q4_prime), .a(convert_bcd_5_a), .b(convert_bcd_5_b),
    .c(convert_bcd_5_c), .d(convert_bcd_5_d), .e(convert_bcd_5_e), .f(convert_bcd_5_f), .g(convert_bcd_5_g));
  convert_bcd convert_bcd_6 (
    .D3(Q3_prime), .D2(Q2_prime), .D1(Q1_prime), .D0(Q0_prime), .a(convert_bcd_6_a), .b(convert_bcd_6_b),
    .c(convert_bcd_6_c), .d(convert_bcd_6_d), .e(convert_bcd_6_e), .f(convert_bcd_6_f), .g(convert_bcd_6_g));
  nor nor_2 (nor_2_out, Q10_prime, Q9_prime, Q8_prime, Q7_prime, Q6_prime, Q5_prime, Q4_prime, Q3_prime, Q2_prime, Q1_prime, Q0_prime);
  _7_Segment_Display #(.active("false")) u_7_segment_display_4 (
    .g(convert_bcd_4_g), .f(convert_bcd_4_f), .a(convert_bcd_4_a), .b(convert_bcd_4_b), .e(convert_bcd_4_e),
    .d(convert_bcd_4_d), .c(convert_bcd_4_c));  // open: dp
  _7_Segment_Display #(.active("false")) u_7_segment_display_5 (
    .g(convert_bcd_5_g), .f(convert_bcd_5_f), .a(convert_bcd_5_a), .b(convert_bcd_5_b), .e(convert_bcd_5_e),
    .d(convert_bcd_5_d), .c(convert_bcd_5_c));  // open: dp
  _7_Segment_Display #(.active("false")) u_7_segment_display_6 (
    .g(convert_bcd_6_g), .f(convert_bcd_6_f), .a(convert_bcd_6_a), .b(convert_bcd_6_b), .e(convert_bcd_6_e),
    .d(convert_bcd_6_d), .c(convert_bcd_6_c));  // open: dp
endmodule

module add_3 (
  input  Q3,
  input  Q2,
  input  Q1,
  input  Q0,
  output Q3N,
  output Q2N,
  output Q1N,
  output Q0N,
  output carry
);

  wire and_1_out, and_2_out, and_3_out, and_4_out, and_5_out, and_6_out, and_7_out, and_8_out, and_9_out,
       not_1_out, not_2_out, not_3_out, not_4_out, not_5_out, not_6_out, not_7_out, not_8_out, not_9_out,
       not_10_out, not_11_out;

  not not_1 (not_1_out, Q1);
  and and_1 (and_1_out, Q2, not_1_out, Q0);
  and and_2 (and_2_out, Q2, Q1, not_2_out);
  not not_2 (not_2_out, Q0);
  not not_3 (not_3_out, Q3);
  not not_4 (not_4_out, Q2);
  and and_3 (and_3_out, not_3_out, not_4_out, Q0);
  not not_5 (not_5_out, Q2);
  and and_4 (and_4_out, not_5_out, Q1);
  and and_5 (and_5_out, Q2, not_6_out, not_7_out);
  not not_6 (not_6_out, Q1);
  not not_7 (not_7_out, Q0);
  not not_8 (not_8_out, Q3);
  and and_6 (and_6_out, not_8_out, not_9_out, not_10_out);
  not not_9 (not_9_out, Q1);
  not not_10 (not_10_out, Q0);
  not not_11 (not_11_out, Q2);
  and and_7 (and_7_out, not_11_out, Q1, Q0);
  and and_8 (and_8_out, Q3, Q0);
  not not_12 (Q0N, Q0);
  and and_9 (and_9_out, Q2, Q1, Q0);
  or or_1 (Q3N, and_1_out, and_2_out);
  or or_2 (Q2N, and_3_out, and_4_out, and_5_out);
  or or_3 (Q1N, and_6_out, and_7_out, and_8_out);
  or or_4 (carry, and_9_out, Q3);
endmodule

module state_update (
  input  Q3,
  input  Q2,
  input  Q1,
  input  Q0,
  output add
);

  wire and_1_out, and_2_out, not_1_out, not_2_out, not_3_out, not_4_out, not_5_out, not_6_out;

  not not_1 (not_1_out, Q3);
  and and_1 (and_1_out, not_1_out, not_2_out, not_3_out);
  not not_2 (not_2_out, Q2);
  not not_3 (not_3_out, Q1);
  not not_4 (not_4_out, Q3);
  and and_2 (and_2_out, not_4_out, not_5_out, not_6_out);
  not not_5 (not_5_out, Q2);
  not not_6 (not_6_out, Q0);
  or or_1 (add, and_1_out, and_2_out);
endmodule

module toogle_sig (
  input  in_1,
  input  in_2,
  output out_3,
  output out_4
);

  wire and_1_out, not_1_out, not_2_out, or_1_out;

  T_Flip_Flop t_ff_1 (.clk(not_1_out), .T(not_1_out), .Q(out_3), .preset(and_1_out), .reset(in_2));  // open: Qn, en
  not not_1 (not_1_out, in_1);
  not not_2 (not_2_out, out_3);
  T_Flip_Flop t_ff_2 (.clk(not_2_out), .T(not_2_out), .Q(out_4), .reset(or_1_out));  // open: Qn, preset, en
  or or_1 (or_1_out, in_2, and_1_out);
  and and_1 (and_1_out, out_4, out_3);
endmodule
